# Fritzing sketch HC-05 y Arduino (saved by Fritzing 0.9.2b)
breadboards: 1

parts:
  Part2 = Bluetooth HC-05 Macho  # not connected
  Parte1 = Arduino Uno (Rev3) - ICSP
  R1 = Resistor [tolerance=±5% resistance=1k package="1206 [SMD]"]
  R2 = Resistor [tolerance=±5% resistance=2.2k package="1206 [SMD]"]

nets:
  N1: Parte1.D11_PWM/MOSI, R1.Pin_1
  N2: Parte1.GND, R2.Pin_0
  N3: R1.Pin_0, R2.Pin_1
