# Fritzing sketch hc-05-serial (saved by Fritzing 0.9.2b)

parts:
  JY-MCU = Arduino Nano (Rev3.0)
  Part1 = Bluetooth HC-05 Macho

nets:
  N1: JY-MCU.D1/TX, Part1.RXD
  N2: JY-MCU.D0/RX, Part1.TXD
  GND: JY-MCU.GND, Part1.GND
  5V: JY-MCU.5V, Part1.VCC
