# Fritzing sketch PWM_LED (saved by Fritzing 0.9.2b)
breadboards: 1

parts:
  Parte1 = Arduino Uno (Rev3) - ICSP
  R1 = Resistor [tolerance=±5% resistance=220 package="1206 [SMD]"]
  LED1 = smd LED [color="Red (633nm)" package="1206 [SMD]"]

nets:
  N1: Parte1.GND, LED1.cathode
  N2: Parte1.D3_PWM, R1.Pin_1
  N3: R1.Pin_0, LED1.anode
