# Fritzing sketch H bride DC motor (saved by Fritzing 0.9.2b)
breadboards: 1

parts:
  S1 = H-Bridge with L298N
  Parte1 = Arduino Uno (Rev3) - ICSP
  M1 = DC Motor  # not connected

nets:
  GND: S1.GND, Parte1.GND
  N1: S1.IN1, Parte1.D3_PWM
  N2: S1.IN2, Parte1.D4

notes:
  GND
  (-)
  7V
  (+)

custom parts:
  H-Bridge with L298N: h-bridge
