# Fritzing sketch DHT11 (saved by Fritzing 0.9.2b)
breadboards: 1

parts:
  DHT1 = DHT11 Humitidy and Temperature Sensor
  Parte1 = Arduino Uno (Rev3) - ICSP
  R1 = Resistor [tolerance=±5% resistance=10k package="2512 [SMD]"]

nets:
  VDD: DHT1.VDD, Parte1.5V, R1.Pin_0
  N1: DHT1.DATA, Parte1.D3_PWM, R1.Pin_1
  GND: DHT1.GND, Parte1.GND

custom parts:
  DHT11 Humitidy and Temperature Sensor: DHT11 Humidity and Temperature Sensor
