# Fritzing sketch Untitled Sketch 2 (saved by Fritzing 0.9.2b)
breadboards: 1

parts:
  T1 = LM35 Temperature Sensor [package="TO92 [THT]"]
  Parte1 = Arduino Uno (Rev3) - ICSP

nets:
  N1: T1.+Vs, Parte1.5V
  N2: T1.Vout, Parte1.A2
  GND: T1.GND, Parte1.GND
