# Fritzing sketch Switch_Button (saved by Fritzing 0.9.2b)
breadboards: 1

parts:
  S1 = Pushbutton [package="[THT]"]
  R3 = Resistor [tolerance=±5% resistance=10k package="0402 [SMD]"]
  Parte1 = Arduino Uno (Rev3) - ICSP
  LED3 = LED - 5mm [color="Red (633nm)" package="5 mm [THT]"]
  R4 = Resistor [tolerance=±5% resistance=220 package="0402 [SMD]"]

nets:
  N1: S1.Pin_1, S1.Pin_2, R3.Pin_0, Parte1.D0/RX
  N2: S1.Pin_3, S1.Pin_4, Parte1.5V
  N3: R3.Pin_1, Parte1.GND, LED3.cathode
  N4: Parte1.D8, R4.Pin_1
  N5: LED3.anode, R4.Pin_0

notes:
  Entradas
  Salidas
